// Logisim project calculadora.circ as structural Verilog
module calculadora (
  input  A,
  input  B,
  input  C,
  input  D,
  output E,
  output F,
  output G,
  output H,
  output I,
  output J,
  output K,
  output L,
  output M,
  output N,
  output O,
  output P,
  output Q,
  output R,
  output S,
  output T,
  output U,
  output V,
  output W,
  output X,
  output Y
);

  wire and_1_out, and_4_out, and_5_out, and_6_out, and_7_out, and_8_out, and_9_out, and_10_out, and_11_out,
       and_12_out, and_13_out, and_14_out, and_15_out, and_16_out, and_17_out, and_18_out, and_19_out,
       and_20_out, and_21_out, and_22_out, and_23_out, and_24_out, and_25_out, and_26_out, and_27_out,
       and_28_out, and_29_out, and_30_out, and_31_out, and_32_out, and_33_out, and_34_out, and_35_out,
       and_36_out, and_37_out, and_38_out, and_39_out, and_40_out, and_41_out, and_42_out, and_43_out,
       and_44_out, and_45_out, and_46_out, and_47_out, and_48_out, and_49_out, and_50_out, and_51_out,
       and_52_out, and_53_out, and_54_out, and_55_out, and_56_out, and_57_out, and_58_out, and_59_out,
       and_60_out, and_61_out, not_1_out, not_2_out, not_3_out, not_4_out, not_6_out, not_7_out, not_8_out,
       not_9_out, not_10_out, not_12_out, not_13_out, not_14_out, not_15_out, not_16_out, not_17_out,
       not_18_out, not_19_out, not_20_out, not_21_out, not_22_out, not_23_out, not_24_out, not_25_out,
       not_26_out, not_27_out, not_28_out, not_29_out, not_30_out, not_31_out, not_32_out, not_33_out,
       not_34_out, not_35_out, not_36_out, not_37_out, not_38_out, not_39_out, not_40_out, not_41_out,
       not_42_out, not_43_out, not_44_out, not_45_out, not_46_out, not_47_out, not_48_out, not_49_out,
       not_50_out, not_51_out, not_52_out, not_53_out, not_54_out, not_55_out, not_56_out, not_57_out,
       not_58_out, or_7_out, or_8_out, or_11_out, or_12_out, or_13_out, or_14_out, or_15_out, or_16_out,
       or_17_out, or_18_out, or_19_out, or_20_out, or_21_out, or_23_out, or_24_out, or_26_out, or_27_out,
       or_28_out, or_29_out, or_30_out;

  not not_1 (not_1_out, B);
  not not_2 (not_2_out, B);
  not not_3 (not_3_out, A);
  not not_4 (not_4_out, B);
  not not_5 (I, B);
  not not_6 (not_6_out, A);
  not not_7 (not_7_out, D);
  not not_8 (not_8_out, D);
  not not_9 (not_9_out, C);
  not not_10 (not_10_out, D);
  not not_11 (P, D);
  not not_12 (not_12_out, C);
  not not_13 (not_13_out, A);
  not not_14 (not_14_out, B);
  not not_15 (not_15_out, A);
  not not_16 (not_16_out, B);
  not not_17 (not_17_out, A);
  not not_18 (not_18_out, C);
  not not_19 (not_19_out, B);
  and and_1 (and_1_out, B, D);
  not not_20 (not_20_out, A);
  not not_21 (not_21_out, B);
  not not_22 (not_22_out, A);
  not not_23 (not_23_out, B);
  not not_24 (not_24_out, A);
  not not_25 (not_25_out, C);
  not not_26 (not_26_out, B);
  not not_27 (not_27_out, A);
  not not_28 (not_28_out, B);
  not not_29 (not_29_out, C);
  not not_30 (not_30_out, D);
  not not_31 (not_31_out, B);
  not not_32 (not_32_out, A);
  not not_33 (not_33_out, B);
  not not_34 (not_34_out, B);
  not not_35 (not_35_out, C);
  not not_36 (not_36_out, A);
  not not_37 (not_37_out, C);
  not not_38 (not_38_out, A);
  not not_39 (not_39_out, C);
  not not_40 (not_40_out, A);
  not not_41 (not_41_out, C);
  not not_42 (not_42_out, A);
  or or_1 (E, not_1_out, A);
  or or_2 (G, not_2_out, A);
  and and_2 (H, not_3_out, not_4_out);
  or or_3 (K, not_6_out, B);
  or or_4 (L, not_7_out, C);
  or or_5 (N, not_8_out, C);
  and and_3 (O, not_9_out, not_10_out);
  or or_6 (R, not_12_out, D);
  and and_4 (and_4_out, not_13_out, not_14_out);
  not not_43 (not_43_out, D);
  and and_5 (and_5_out, not_15_out, C);
  not not_44 (not_44_out, D);
  and and_6 (and_6_out, not_16_out, C);
  and and_7 (and_7_out, not_17_out, B);
  and and_8 (and_8_out, not_18_out, D);
  and and_9 (and_9_out, A, not_19_out);
  not not_45 (not_45_out, C);
  and and_10 (and_10_out, A, B);
  not not_46 (not_46_out, D);
  or or_7 (or_7_out, C, and_1_out);
  and and_11 (and_11_out, not_20_out, not_21_out);
  not not_47 (not_47_out, D);
  and and_12 (and_12_out, not_22_out, C);
  not not_48 (not_48_out, D);
  and and_13 (and_13_out, not_23_out, C);
  and and_14 (and_14_out, not_24_out, B);
  and and_15 (and_15_out, not_25_out, D);
  and and_16 (and_16_out, A, not_26_out);
  not not_49 (not_49_out, C);
  and and_17 (and_17_out, A, B);
  not not_50 (not_50_out, D);
  and and_18 (and_18_out, not_27_out, not_28_out);
  and and_19 (and_19_out, not_29_out, not_30_out);
  and and_20 (and_20_out, B, C);
  and and_21 (and_21_out, A, not_31_out);
  and and_22 (and_22_out, A, B);
  and and_23 (and_23_out, not_32_out, not_33_out);
  not not_51 (not_51_out, D);
  and and_24 (and_24_out, not_34_out, not_35_out);
  not not_52 (not_52_out, D);
  and and_25 (and_25_out, not_36_out, B);
  and and_26 (and_26_out, not_37_out, D);
  and and_27 (and_27_out, A, B);
  or or_8 (or_8_out, not_38_out, not_39_out);
  not not_53 (not_53_out, D);
  and and_28 (and_28_out, not_40_out, not_41_out);
  not not_54 (not_54_out, D);
  not not_55 (not_55_out, B);
  not not_56 (not_56_out, C);
  and and_29 (and_29_out, not_42_out, B);
  not not_57 (not_57_out, B);
  and and_30 (and_30_out, and_4_out, not_43_out);
  and and_31 (and_31_out, and_5_out, not_44_out);
  and and_32 (and_32_out, and_6_out, D);
  and and_33 (and_33_out, and_7_out, and_8_out);
  and and_34 (and_34_out, and_9_out, not_45_out);
  and and_35 (and_35_out, and_10_out, not_46_out);
  and and_36 (and_36_out, A, B);
  or or_9 (T, or_7_out, A);
  and and_37 (and_37_out, and_11_out, not_47_out);
  and and_38 (and_38_out, and_12_out, not_48_out);
  and and_39 (and_39_out, and_13_out, D);
  and and_40 (and_40_out, and_14_out, and_15_out);
  and and_41 (and_41_out, and_16_out, not_49_out);
  and and_42 (and_42_out, and_17_out, not_50_out);
  and and_43 (and_43_out, A, B);
  and and_44 (and_44_out, and_18_out, and_19_out);
  and and_45 (and_45_out, and_20_out, D);
  and and_46 (and_46_out, and_21_out, C);
  and and_47 (and_47_out, and_22_out, D);
  and and_48 (and_48_out, and_23_out, not_51_out);
  and and_49 (and_49_out, and_24_out, not_52_out);
  and and_50 (and_50_out, and_25_out, and_26_out);
  and and_51 (and_51_out, and_27_out, C);
  or or_10 (X, or_8_out, not_53_out);
  and and_52 (and_52_out, and_28_out, not_54_out);
  and and_53 (and_53_out, not_55_out, D);
  and and_54 (and_54_out, B, not_56_out);
  not not_58 (not_58_out, D);
  and and_55 (and_55_out, and_29_out, C);
  and and_56 (and_56_out, A, D);
  and and_57 (and_57_out, A, not_57_out);
  or or_11 (or_11_out, and_30_out, and_31_out);
  or or_12 (or_12_out, or_11_out, or_13_out);
  or or_13 (or_13_out, and_32_out, and_33_out);
  or or_14 (or_14_out, and_34_out, and_35_out);
  or or_15 (or_15_out, or_14_out, and_58_out);
  and and_58 (and_58_out, and_36_out, C);
  or or_16 (or_16_out, and_37_out, and_38_out);
  or or_17 (or_17_out, or_16_out, or_18_out);
  or or_18 (or_18_out, and_39_out, and_40_out);
  or or_19 (or_19_out, and_41_out, and_42_out);
  or or_20 (or_20_out, or_19_out, and_59_out);
  and and_59 (and_59_out, and_43_out, C);
  or or_21 (or_21_out, and_44_out, and_45_out);
  or or_22 (V, or_21_out, or_23_out);
  or or_23 (or_23_out, and_46_out, and_47_out);
  or or_24 (or_24_out, and_48_out, and_49_out);
  or or_25 (W, or_24_out, or_26_out);
  or or_26 (or_26_out, and_50_out, and_51_out);
  or or_27 (or_27_out, and_52_out, and_53_out);
  or or_28 (or_28_out, or_27_out, and_60_out);
  and and_60 (and_60_out, and_54_out, not_58_out);
  or or_29 (or_29_out, and_55_out, and_56_out);
  or or_30 (or_30_out, or_29_out, and_61_out);
  and and_61 (and_61_out, and_57_out, C);
  or or_31 (S, or_12_out, or_15_out);
  or or_32 (U, or_17_out, or_20_out);
  or or_33 (Y, or_28_out, or_30_out);

  assign F = A;
  assign J = 1'b1;
  assign M = C;
  assign Q = 1'b1;
endmodule
